// Digital circuit dffRopt.dig as structural Verilog
module dffRopt (
  input  D,
  input  C,
  input  R,
  output Q,
  output Q_2
);

  wire nfet_2_s, nfet_5_s, R_t, RESET, RESET_t, SET, SET_t;

  NFET nfet_1 (.G(R), .D(R_t), .S(1'b0));
  PullUp pullup_1 (.out(SET_t));
  s2 s2_1 (._1(SET), ._2(C), .D(SET_t), .S(R_t));
  PullUp pullup_2 (.out(RESET_t));
  NFET nfet_2 (.G(D), .D(RESET_t), .S(nfet_2_s));
  NFET nfet_3 (.G(Q), .D(Q_2), .S(nfet_2_s));
  NFET nfet_4 (.G(RESET), .D(nfet_2_s), .S(R_t));
  PullUp pullup_3 (.out(Q_2));
  PullUp pullup_4 (.out(RESET));
  s2 s2_2 (._1(C), ._2(RESET_t), .D(RESET), .S(nfet_5_s));
  PullUp pullup_5 (.out(SET));
  NFET nfet_5 (.G(RESET_t), .D(SET), .S(nfet_5_s));
  NFET nfet_6 (.G(SET_t), .D(nfet_5_s), .S(1'b0));
  PullUp pullup_6 (.out(Q));
  NFET nfet_7 (.G(Q_2), .D(Q), .S(nfet_5_s));

  // Other names for the same wires on the sheet: Q_t = Q_2

  // Notes on the sheet:
  //   R: default 1
endmodule
