// Digital circuit computer_toy.dig as structural Verilog
module computer_toy (
  input  Load_ACC,
  input  Load_H,
  input  In_0,
  input  In_1,
  input  In_2,
  input  In_3,
  input  In_4,
  input  In_5,
  input  In_6,
  input  In_7,
  input  Load_In,
  input  Load_M,
  input  Load_L,
  input  [7:0] Carry,
  input  _0,
  input  _1,
  input  _1_2,
  input  X,
  input  Y,
  input  X_2,
  input  Y_2,
  input  X_plus_1,
  input  Y_plus_1,
  input  X_3,
  input  Y_3,
  input  X_1,
  input  Y_1,
  input  X_plus_Y,
  input  X_Y,
  input  Y_X,
  input  Y_X_2,
  input  Y_X_3,
  input  Load_ROM,
  input  Load_PC_H,
  input  Load_PC_L,
  output [7:0] ALU,
  output [7:0] D,
  output [7:0] ACC,
  output [7:0] H,
  output [7:0] In,
  output [7:0] Bus,
  output [7:0] M,
  output [7:0] L,
  output [15:0] A,
  output [15:0] PC,
  output [7:0] ROM,
  output [7:0] PC_H,
  output [7:0] PC_L
);

  wire nm_alu_hack8_1_c_out, nm_alu_hack8_1_ng, nm_alu_hack8_1_zr, nm_hack_opflag_decoder_1_f,
       nm_hack_opflag_decoder_1_no, nm_hack_opflag_decoder_1_nx, nm_hack_opflag_decoder_1_ny,
       nm_hack_opflag_decoder_1_zx, nm_hack_opflag_decoder_1_zy, Reset_out, Save_ACC_out, Set_D_out,
       Set_H_out, Set_L_out, Set_M_out, Set_PC_H_out, Set_PC_L_out, Set_PC_out;
  wire [7:0] nm_byte_resetn_1_out;

  Button Set_PC_H (.out(Set_PC_H_out));
  Button Set_PC_L (.out(Set_PC_L_out));
  Button Set_PC (.out(Set_PC_out));
  nm_reg8_resetn nm_reg8_resetn_1 (.D(Bus), .clk(Set_PC_H_out), .reset(Reset_out), .en(Load_PC_H), .Out(Bus), .V(PC_H));
  nm_reg8_resetn nm_reg8_resetn_2 (.D(Bus), .clk(Set_PC_L_out), .reset(Reset_out), .en(Load_PC_L), .Out(Bus), .V(PC_L));
  Button #(.activeLow("true")) Reset (.out(Reset_out));
  nm_byte2_resetn nm_byte2_resetn_1 (.D({PC_H, PC_L}), .clk(Set_PC_out), .reset(Reset_out), .Out(PC));  // open: Out_2
  nm_enable8 nm_enable8_1 (.In({In_7, In_6, In_5, In_4, In_3, In_2, In_1, In_0}), .en(Load_In), .Out(Bus));
  ROM #(.AddrBits(16), .Bits(8)) rom_1 (.A(PC), .sel(1'b1), .D(ROM));
  nm_enable8 nm_enable8_2 (.In(ROM), .en(Load_ROM), .Out(Bus));
  Button Set_D (.out(Set_D_out));
  nm_byte_resetn nm_byte_resetn_1 (
    .D(Bus), .clk(Set_D_out), .reset(Reset_out), .Out(nm_byte_resetn_1_out));  // open: Out_2
  nm_ALU_HACK8 nm_alu_hack8_1 (
    .X(nm_byte_resetn_1_out), .Y(Bus), .c_in(Carry), .Out(ALU), .zr(nm_alu_hack8_1_zr),
    .ng(nm_alu_hack8_1_ng), .c_out(nm_alu_hack8_1_c_out), .zx(nm_hack_opflag_decoder_1_zx),
    .nx(nm_hack_opflag_decoder_1_nx), .zy(nm_hack_opflag_decoder_1_zy), .ny(nm_hack_opflag_decoder_1_ny),
    .f(nm_hack_opflag_decoder_1_f), .no(nm_hack_opflag_decoder_1_no));
  nm_HACK_opflag_decoder nm_hack_opflag_decoder_1 (
    ._0(_0), ._1(_1), ._1_2(_1_2), .X(X), .Y(Y), .X_2(X_2), .Y_2(Y_2), .X_3(X_3), .Y_3(Y_3),
    .X_plus_1(X_plus_1), .Y_plus_1(Y_plus_1), .X_1(X_1), .Y_1(Y_1), .X_plus_Y(X_plus_Y), .X_Y(X_Y),
    .Y_X(Y_X), .Y_X_2(Y_X_2), .Y_X_3(Y_X_3), .zx(nm_hack_opflag_decoder_1_zx),
    .nx(nm_hack_opflag_decoder_1_nx), .zy(nm_hack_opflag_decoder_1_zy), .ny(nm_hack_opflag_decoder_1_ny),
    .f(nm_hack_opflag_decoder_1_f), .no(nm_hack_opflag_decoder_1_no));
  LED Zero (.in(nm_alu_hack8_1_zr));
  LED Negative (.in(nm_alu_hack8_1_ng));
  LED u_Carry (.in(nm_alu_hack8_1_c_out));
  Button Save_ACC (.out(Save_ACC_out));
  Button Set_H (.out(Set_H_out));
  Button Set_L (.out(Set_L_out));
  nm_reg8_resetn nm_reg8_resetn_3 (.D(ALU), .clk(Save_ACC_out), .reset(Reset_out), .en(Load_ACC), .Out(Bus), .V(ACC));
  nm_reg8_resetn nm_reg8_resetn_4 (.D(Bus), .clk(Set_H_out), .reset(Reset_out), .en(Load_H), .Out(Bus), .V(A[15:8]));
  nm_reg8_resetn nm_reg8_resetn_5 (.D(Bus), .clk(Set_L_out), .reset(Reset_out), .en(Load_L), .Out(Bus), .V(A[7:0]));
  RAMAsync #(.AddrBits(16), .Bits(8)) ramasync_1 (.A(A), .D(Bus), .we(Set_M_out), .Q(M));
  Button Set_M (.out(Set_M_out));
  nm_enable8 nm_enable8_3 (.In(M), .en(Load_M), .Out(Bus));
  // Pins of 1 and 8 bits meet at Carry

  assign D = Bus;
  assign H = A[15:8];
  assign In = {In_7, In_6, In_5, In_4, In_3, In_2, In_1, In_0};
  assign L = A[7:0];

  // Notes on the sheet:
  //   X_plus_Y: default 1
  //   contents of rom_1 (hex, n*v repeats v):
  //   de,ad,be,ef
endmodule
