// Digital circuit nm_Xor.dig as structural Verilog
module nm_Xor (
  input  In_1,
  input  In_2,
  output Out
);

  wire nm_not_1_out, nm_not_2_out;

  nm_not nm_not_1 (.In(In_1), .Out(nm_not_1_out));
  nm_not nm_not_2 (.In(In_2), .Out(nm_not_2_out));
  // nm_aoi2x2 nm_aoi2x2_1: pin names not known; wires that end beside it: In_2, In_1, nm_not_1_out, nm_not_2_out, Out
endmodule
