// Digital circuit nm_dff_asyncn.dig as structural Verilog
module nm_dff_asyncn (
  input  D,
  input  clk,
  input  r,
  input  s,
  output Q,
  output Q_2
);

  wire nm_not_1_out;

  nm_not nm_not_1 (.In(D), .Out(nm_not_1_out));
  nm_jk_asyncn nm_jk_asyncn_1 (.J(D), .clk(clk), .r(r), .s(s), .K(nm_not_1_out), .Q(Q), .Q_2(Q_2));
endmodule
