// Digital circuit nm_mux.dig as structural Verilog
module nm_mux (
  input  In_1,
  input  sel,
  input  In_2,
  output Out
);

  wire nm_muxn_1_out;

  nm_muxn nm_muxn_1 (.In_1(In_1), .In_2(In_2), .sel(sel), .Out(nm_muxn_1_out));
  nm_not nm_not_1 (.In(nm_muxn_1_out), .Out(Out));
endmodule
